# Fritzing sketch matrix-wait-bus-time (saved by Fritzing 0.9.3b)

parts:
  WeMos_D1_R1 = WeMos D1 R2
  Composant1 = Matrix LED de 8x8 basada en MAX7219

nets:
  N1: WeMos_D1_R1.(D5), Composant1.CS
  N2: WeMos_D1_R1.(D6), Composant1.CLK
  N3: WeMos_D1_R1.(D7), Composant1.DIN
  GND: WeMos_D1_R1.GND, Composant1.GND
  5V: WeMos_D1_R1.5V, Composant1.VCC

custom parts:
  WeMos D1 R2: The D1 R2 is a mini wifi board based on the ESP-8266EX.
